# Fritzing sketch circuit (saved by Fritzing 0.9.2b)
breadboards: 1

parts:
  부품1 = Arduino Uno (Rev3)
  U1 = L9110 H-bridge module [part_number="L9110 H-bridge"]
  DC_Mot_Enc1 = DC Motor with two-phase hall-encoder [part_number=VT-E-G25A-06-177E]
  VCC1 = 4 x AAA Battery Mount  # not connected

nets:
  N1: 부품1.D2, DC_Mot_Enc1.pin3
  N2: 부품1.D4, DC_Mot_Enc1.pin4
  N3: 부품1.D5_PWM, U1.A-IA
  N4: 부품1.D6_PWM, U1.A-IB
  5V: 부품1.5V, U1.VCC, DC_Mot_Enc1.pin2
  GND: 부품1.GND, U1.GND, DC_Mot_Enc1.pin5
  N5: U1.MOTOR_A-A, DC_Mot_Enc1.pin6
  N6: U1.MOTOR_A-B, DC_Mot_Enc1.pin1
